// Logisim project ModuloOrdenador.circ as structural Verilog: 1 circuit, main circuit Módulo Ordenador
module \Módulo_Ordenador  (
  input  [31:0] Datos_ROM,
  input  Reloj,
  input  Activo,
  output [14:0] \Dirección_ROM ,
  output Activa_RAM,
  output [14:0] \Dirección_RAM ,
  output [16:0] Datos_RAM,
  output Fin
);

  wire [31:0] Ceros_q;

  Counter #(.width(15), .max('h7fff)) counter_1 (
    .count(Activo), .Q(\Dirección_ROM ), .carry(Fin), .clk(Reloj));  // open: load, D, clr, preset, down
  Register #(.width(32)) Ceros (.Q(Ceros_q), .clk(Reloj));  // open: D, en, clr
  Comparator #(.width(32), .mode("unsigned")) comparator_1 (
    .a(Datos_ROM), .b(Ceros_q), .eq(Activa_RAM));  // open: gt, lt

  assign Datos_RAM = Datos_ROM[16:0];
  assign \Dirección_RAM  = Datos_ROM[31:17];

  // Other names for the same wires on the sheet: Act_RAM = Activa_RAM; Dat_RAM[16:0] = Datos_ROM[16:0];
  //   Dat_ROM[31:0] = Datos_ROM; Dir_RAM[14:0] = Datos_ROM[31:17]; Dir_ROM[14:0] = \Dirección_ROM 

  // Notes on the sheet:
  //   Entradas
  //   Sección 1
  //   Sección 2
  //   Sección 3
  //   Salidas
endmodule
