// Logisim project OrdenadorPrueba.circ as structural Verilog: 1 circuit, main circuit main
module main (
  input  in_1
);

  wire clock_1_out, not_1_out, Ordenador_activa_ram, Ordenador_fin;
  wire [14:0] \Ordenador_dirección_ram , \Ordenador_dirección_rom ;
  wire [16:0] Ordenador_datos_ram;
  wire [31:0] rom_1_data;

  ROM #(.addrWidth(15), .dataWidth(32)) rom_1 (.addr(\Ordenador_dirección_rom ), .data(rom_1_data));
  not not_1 (not_1_out, Ordenador_fin);
  Clock clock_1 (.out(clock_1_out));
  \Módulo_Ordenador  Ordenador (
    .Datos_ROM(rom_1_data), .Reloj(clock_1_out), .Activo(not_1_out),
    .\Dirección_ROM (\Ordenador_dirección_rom ), .Activa_RAM(Ordenador_activa_ram),
    .\Dirección_RAM (\Ordenador_dirección_ram ), .Datos_RAM(Ordenador_datos_ram), .Fin(Ordenador_fin));
  RAM #(.addrWidth(15), .dataWidth(17)) ram_1 (
    .addr(\Ordenador_dirección_ram ), .data(Ordenador_datos_ram), .sel(Ordenador_activa_ram),
    .clk(clock_1_out), .ld(in_1));  // open: clr

  // Notes on the sheet:
  //   contents of rom_1 (hex, n*v repeats v):
  //   40008 8001 30000 8003 32763*0 8007
endmodule
