// Logisim project TuringMac.circ as structural Verilog: 1 circuit, main circuit Maquina de turing
module Maquina_de_turing (
  input  [1:0] in_1,
  output out_2
);

  wire Activador, B_Trigg, clock_1_out, d_ff_1_qn, D_Trigg, direccion_1_out_3, direccion_1_out_4, E_Trigg,
       Fin, not_1_out, or_1_out, RamII_Trig, S_Trigg;
  wire [6:0] RAM_I_data, Symbol_q;
  wire [9:0] RAM_PTR_q;
  wire [14:0] RAM_II_ADDR, ROM_ADDR;
  wire [16:0] RAM_II_DATA;
  wire [31:0] ROM_DATA;

  Clock clock_1 (.out(clock_1_out));
  D_Flip_Flop #(.Pre_Clr_Positions("LEGACY"), .enable("true"), .NewFFLayout("false")) d_ff_1 (
    .clk(Fin), .D(Fin), .Qn(d_ff_1_qn));  // open: Q, preset, en, reset
  Direccion direccion_1 (.in_1(in_1), .out_2(out_2), .out_3(direccion_1_out_3), .out_4(direccion_1_out_4));
  Control control_1 (
    .in_1(clock_1_out), .in_2(Fin), .out_3(S_Trigg), .out_4(B_Trigg), .out_5(E_Trigg), .out_6(D_Trigg));
  \Módulo_Ordenador  \módulo_ordenador_1  (
    .Datos_ROM(ROM_DATA), .Reloj(clock_1_out), .Activo(d_ff_1_qn), .\Dirección_ROM (ROM_ADDR),
    .Activa_RAM(Activador), .\Dirección_RAM (RAM_II_ADDR), .Datos_RAM(RAM_II_DATA), .Fin(Fin));
  ROM #(.addrWidth(15), .dataWidth(32)) ROM (.addr(ROM_ADDR), .data(ROM_DATA));
  not not_1 (not_1_out, direccion_1_out_4);
  Counter #(.width(10), .max('h3ff)) RAM_PTR (
    .count(not_1_out), .Q(RAM_PTR_q), .clk(clock_1_out), .down(direccion_1_out_3));  // open: load, D, carry, clr, preset
  RAM #(.addrWidth(10), .dataWidth(7)) RAM_I (
    .addr(RAM_PTR_q), .data(RAM_I_data), .clk(clock_1_out), .ld(E_Trigg));  // open: sel, clr
  Register #(.width(7)) Symbol (.D(RAM_I_data), .en(S_Trigg), .Q(Symbol_q), .clk(clock_1_out));  // open: clr
  or or_1 (or_1_out, Activador, RamII_Trig);
  RAM #(.addrWidth(15), .dataWidth(17)) RAM_II (
    .addr(RAM_II_ADDR), .data(RAM_II_DATA), .sel(or_1_out));  // open: clk, ld, clr
  Register #(.width(17)) IBR (.D(RAM_II_DATA));  // open: en, Q, clk, clr
  Register State ();  // open: D, en, Q, clk, clr

  // Notes on the sheet:
  //   Init Lock
  //   Aqui muere
endmodule
