// Logisim project Control.circ as structural Verilog: 1 circuit, main circuit Control
module Control (
  input  in_1,
  input  in_2,
  output out_3,
  output out_4,
  output out_5,
  output out_6
);

  wire controlled_buffer_1_out, d_ff_1_q;
  wire [1:0] counter_1_q;

  assign controlled_buffer_1_out = d_ff_1_q ? in_1 : 1'bz;  // Controlled_Buffer controlled_buffer_1
  D_Flip_Flop #(.Pre_Clr_Positions("LEGACY"), .enable("true"), .NewFFLayout("false")) d_ff_1 (
    .clk(in_2), .D(in_2), .Q(d_ff_1_q));  // open: Qn, preset, en, reset
  Decoder #(.select(2), .enable("false")) decoder_1 (
    .out0(out_3), .out1(out_4), .out2(out_5), .out3(out_6), .sel(counter_1_q));
  Counter #(.width(2), .max('h3), .behavior("old")) counter_1 (
    .Q(counter_1_q), .clk(controlled_buffer_1_out));  // open: load, D, count, carry, clr, preset
endmodule
