// Logisim project Direcion.circ as structural Verilog: 1 circuit, main circuit Direccion
module Direccion (
  input  [1:0] in_1,
  output out_2,
  output out_3,
  output out_4
);

  Decoder #(.select(2), .enable("false")) decoder_1 (
    .out0(out_2), .out1(out_3), .out3(out_4), .sel(in_1));  // open: out2
endmodule
