// Logisim project Maquina.circ as structural Verilog: 1 circuit, main circuit main
module main (
  input  in_1
);

  wire Act_RAM, Act_RAM_Ord, and_2_out, and_4_out, Arranque, Btn_Der, Btn_Izq, clock_1_out, counter_2_carry,
       d_ff_1_qn, Etapa_0, Etapa_1, Etapa_2, Etapa_3, Fin_Ord, Izquierda, Muere, nand_1_out, not_1_out,
       not_2_out, not_3_out, not_5_out, or_1_out, or_2_out, or_3_out, Quieto, Reloj, Vive;
  wire [1:0] Direccion;
  wire [6:0] Sim_Prox;
  wire [7:0] Est_Prox;
  wire [9:0] Pos_Actual;
  wire [14:0] Dir_RAM, Dir_RAM_Ord, Dir_RAM_UC, Dir_ROM;
  wire [16:0] Dat_RAM, Dat_RAM_Ord;
  wire [16:10] Inst_Actual;
  wire [31:0] Dat_ROM;

  Clock clock_1 (.out(clock_1_out));
  and and_1 (Reloj, Vive, clock_1_out);
  Register Estado_actual (.D(Est_Prox), .en(Etapa_2), .Q(Dir_RAM_UC[14:7]), .clk(Reloj));  // open: clr
  \Módulo_Ordenador  \módulo_ordenador_1  (
    .Datos_ROM(Dat_ROM), .Reloj(Reloj), .Activo(d_ff_1_qn), .\Dirección_ROM (Dir_ROM),
    .Activa_RAM(Act_RAM_Ord), .\Dirección_RAM (Dir_RAM_Ord), .Datos_RAM(Dat_RAM_Ord), .Fin(Fin_Ord));
  D_Flip_Flop #(.Pre_Clr_Positions("LEGACY"), .enable("true"), .NewFFLayout("false")) d_ff_1 (
    .clk(Fin_Ord), .D(Fin_Ord), .Qn(d_ff_1_qn));  // open: Q, preset, en, reset
  Button Mover_a_la_izquierda (.out(Btn_Izq));
  ROM #(.addrWidth(15), .dataWidth(32)) ROM (.addr(Dir_ROM), .data(Dat_ROM));
  Control control_1 (.in_1(Reloj), .in_2(Fin_Ord), .out_3(Etapa_0), .out_4(Etapa_1), .out_5(Etapa_2), .out_6(Etapa_3));
  Register #(.width(7)) \Símbolo_actual  (.D(Sim_Prox), .en(Etapa_0), .Q(Dir_RAM_UC[6:0]), .clk(Reloj));  // open: clr
  Button Mover_a_la_derecha (.out(Btn_Der));
  // DipSwitch #(.NSwitches(1)) dipswitch_1: pin names not known; wires that end beside it: Arranque
  Register #(.width(17)) IBR (
    .D(Dat_RAM), .en(Etapa_1), .Q({Inst_Actual, Direccion, Est_Prox}), .clk(Reloj));  // open: clr
  not not_1 (not_1_out, Etapa_1);
  not not_2 (not_2_out, Quieto);
  and and_2 (and_2_out, not_2_out, Etapa_3);
  Multiplexer #(.width(15), .enable("false")) multiplexer_1 (
    .in0(Dir_RAM_Ord), .in1(Dir_RAM_UC), .out(Dir_RAM), .sel(Fin_Ord));
  and and_3 (Act_RAM, Act_RAM_Ord, not_1_out);
  or or_1 (or_1_out, Btn_Der, Btn_Izq, and_2_out);
  or or_2 (or_2_out, Izquierda, Btn_Izq);
  or or_3 (or_3_out, Reloj, Btn_Izq, Btn_Der);
  Direccion direccion_1 (.in_1(Direccion), .out_2(Muere), .out_3(Izquierda), .out_4(Quieto));
  Counter #(.width(10), .max('h3ff)) counter_1 (
    .count(or_1_out), .Q(Pos_Actual), .clk(or_3_out), .down(or_2_out));  // open: load, D, carry, clr, preset
  Counter #(.width(2), .max('h2)) counter_2 (
    .carry(counter_2_carry), .clk(and_4_out));  // open: load, D, count, Q, clr, preset, down
  and and_4 (and_4_out, Muere, Arranque);
  not not_3 (not_3_out, Fin_Ord);
  assign Dat_RAM = not_3_out ? Dat_RAM_Ord : 17'bz;  // Controlled_Buffer controlled_buffer_1
  RAM #(.addrWidth(15), .dataWidth(17)) RAM_ROM (
    .addr(Dir_RAM), .data(Dat_RAM), .sel(Act_RAM), .clk(Reloj), .ld(Fin_Ord));  // open: clr
  not not_4 (Vive, counter_2_carry);
  not not_5 (not_5_out, Vive);
  LED Terminado (.in(not_5_out));
  DotMatrix #(.matrixcols(7), .matrixrows(1)) dotmatrix_1 (
    .col0(Dir_RAM_UC[6]), .col1(Dir_RAM_UC[5]), .col2(Dir_RAM_UC[4]), .col3(Dir_RAM_UC[3]),
    .col4(Dir_RAM_UC[2]), .col5(Dir_RAM_UC[1]), .col6(Dir_RAM_UC[0]));
  nand nand_1 (nand_1_out, Etapa_2, Fin_Ord);
  assign Sim_Prox = Etapa_2 ? Inst_Actual : 7'bz;  // Controlled_Buffer controlled_buffer_2
  RAM #(.addrWidth(10), .dataWidth(7)) Cinta (
    .addr(Pos_Actual), .data(Sim_Prox), .clk(Reloj), .ld(nand_1_out));  // open: sel, clr

  // Other names for the same wires on the sheet: Sim_Actual[6:0] = Dir_RAM_UC[6:0];
  //   Est_Actual[7:0] = Dir_RAM_UC[14:7]; Inst_Actual[9:0] = {Direccion, Est_Prox}; Sim_Esc[6:0] = Inst_Actual

  // Notes on the sheet:
  //   Para no ejecutar el ordenador completo:
  //   1) Cargue una RAM ordenada o ejecute el ordenador hasta el fin de las instrucciones en ROM
  //   2) Desconecte "Fin Ord" del módulo ordenador
  //   3) Conecte y active este pin
endmodule
